# Fritzing sketch f330D_RRefactored__bb0b (saved by Fritzing 0.9.0b)
breadboards: 3

parts:
  IC1 = IC, DIP package, 20 pins [chip_label=C8051F330D]
  IC2 = IC, DIP package, 20 pins [chip_label=C8051F330D]
  IC3 = IC, DIP package, 10 pins [chip_label=PiUART]
  R1 = Resistor [tolerance=±5% resistance=1k package=THT]
  D1 = Rectifier Diode [part_number=1N4148 package="300 mil [THT]"]
  S1 = Pushbutton [package="[THT]"]
  C1 = Ceramic Capacitor [capacitance=100nF package="100 mil [THT, multilayer]"]
  R2 = Resistor [tolerance=±5% resistance=100k package=THT]

nets:
  N1: IC1.pin5, IC2.pin5, IC3.pin8, S1.Pin_1, S1.Pin_2, C1.1
  N2: IC1.pin6, IC2.pin6, R1.Pin_1, D1.cathode, R2.Pin_0
  N3: IC1.pin17, IC2.pin7, R1.Pin_0, D1.anode, S1.Pin_3, S1.Pin_4, C1.0, R2.Pin_1
  N4: IC1.pin18, IC2.pin8
  N5: IC2.pin19, IC3.pin6
  N6: IC2.pin20, IC3.pin7

notes:
  3.3 VDC
  N.C.
  P0.7
  P0.5
  P0.3
  P0.1
  C2CLK
  1
  7
  8
  14
  GND
  P0.6
  P0.4
  P0.2
  P0.0
  /RST
  JTAG/C2
  (lower header)
  (upper header)
  APPLICATION
  TODO: Map TX and RX PiUART to correct MCU pins
  C2CK
  C2D
  C8051F330 JTAG/C2, CP2104 USB-UART * C2CK tolerant /RST circuit, bb0b
