# Fritzing sketch f330D_RRefactored__bb2a (saved by Fritzing 0.9.0b)
breadboards: 3

parts:
  IC1 = IC, DIP package, 20 pins [chip_label=C8051F330D]
  IC2 = IC, DIP package, 20 pins [chip_label=C8051F330D]
  IC3 = IC, DIP package, 10 pins [chip_label=PiUART]
  R2 = Resistor [tolerance=±5% resistance=1k package=THT]
  D1 = Rectifier Diode [part_number=1N4148 package="300 mil [THT]"]
  S1 = Pushbutton [package="[THT]"]
  C1 = Ceramic Capacitor [capacitance=100nF package="100 mil [THT, multilayer]"]
  R3 = Resistor [tolerance=±5% resistance=100k package=THT]
  R1 = Resistor [tolerance=±5% resistance=1k package=THT]
  C2 = Ceramic Capacitor [capacitance=100nF package="100 mil [THT, multilayer]"]
  C3 = Ceramic Capacitor [capacitance=100nF package="100 mil [THT, multilayer]"]
  C4 = Ceramic Capacitor [capacitance=100nF package="100 mil [THT, multilayer]"]
  C5 = Ceramic Capacitor [capacitance=100nF package="100 mil [THT, multilayer]"]
  C6 = Ceramic Capacitor [capacitance=100nF package="100 mil [THT, multilayer]"]
  C7 = Ceramic Capacitor [capacitance=100nF package="100 mil [THT, multilayer]"]
  C8 = Ceramic Capacitor [capacitance=100nF package="100 mil [THT, multilayer]"]
  C9 = Ceramic Capacitor [capacitance=100nF package="100 mil [THT, multilayer]"]
  C10 = Ceramic Capacitor [capacitance=100nF package="100 mil [THT, multilayer]"]
  C11 = Ceramic Capacitor [capacitance=100nF package="100 mil [THT, multilayer]"]

nets:
  N1: IC1.pin5, IC2.pin5, IC3.pin8, S1.Pin_1, S1.Pin_2, C1.1, C2.0, C3.0, C4.0, C5.0, C6.0, C7.0, C8.0, C9.0, C10.0, C11.0
  N2: IC1.pin6, IC2.pin6, R2.Pin_1, D1.cathode, R3.Pin_0
  N3: IC1.pin17, IC2.pin7, R1.Pin_0
  N4: IC1.pin18, IC2.pin8
  N5: IC2.pin19, IC3.pin6
  N6: IC2.pin20, IC3.pin7
  N7: R2.Pin_0, D1.anode, S1.Pin_3, S1.Pin_4, C1.0, R3.Pin_1, R1.Pin_1, C2.1, C3.1, C4.1, C5.1, C6.1, C7.1, C8.1, C9.1, C10.1, C11.1

notes:
  3.3 VDC
  N.C.
  P0.7
  P0.5
  P0.3
  P0.1
  C2CLK
  1
  7
  8
  14
  GND
  P0.6
  P0.4
  P0.2
  P0.0
  /RST
  JTAG/C2
  (lower header)
  (upper header)
  APPLICATION
  TODO: Map TX and RX PiUART to correct MCU pins
  C2CK
  C2D
  C8051F330 JTAG/C2, CP2104 USB-UART * C2CK tolerant /RST circuit, bb2a
