# Fritzing sketch f330D_Refactored__aa1f (saved by Fritzing 0.9.0b)
breadboards: 1

parts:
  J2 = female pin header, 7 pins [form="♀ (female)"]
  J1 = female pin header, 7 pins [form="♀ (female)"]
  J4 = female pin header, 7 pins [form="♀ (female)"]
  J3 = female pin header, 7 pins [form="♀ (female)"]
  IC1 = IC, DIP package, 20 pins [chip_label=C8051F330D]
  IC2 = IC, DIP package, 20 pins [chip_label=C8051F330D]
  D1 = Rectifier Diode [part_number=1N4148 package="300 mil [THT]"]
  D2 = Rectifier Diode [part_number=1N4148 package="300 mil [THT]"]
  D3 = Rectifier Diode [part_number=1N4148 package="300 mil [THT]"]
  D4 = Rectifier Diode [part_number=1N4148 package="300 mil [THT]"]
  D5 = Rectifier Diode [part_number=1N4148 package="300 mil [THT]"]
  D6 = Rectifier Diode [part_number=1N4148 package="300 mil [THT]"]
  D7 = Rectifier Diode [part_number=1N4148 package="300 mil [THT]"]
  D8 = Rectifier Diode [part_number=1N4148 package="300 mil [THT]"]
  D9 = Rectifier Diode [part_number=1N4148 package="300 mil [THT]"]
  D10 = Rectifier Diode [part_number=1N4148 package="300 mil [THT]"]
  D11 = Rectifier Diode [part_number=1N4148 package="300 mil [THT]"]
  D12 = Rectifier Diode [part_number=1N4148 package="300 mil [THT]"]
  IC3 = IC, DIP package, 10 pins [chip_label=PiUART]
  J5 = female pin header, 7 pins [form="♀ (female)"]  # not connected
  J6 = female pin header, 7 pins [form="♀ (female)"]  # not connected

nets:
  N1: J2.pin4, IC2.pin19, D11.cathode, D12.anode
  N2: J1.pin5, IC2.pin20, D9.cathode, D10.anode
  N3: J4.pin5, IC1.pin20, D1.cathode, D2.anode
  N4: J4.pin6, IC1.pin18, IC2.pin8
  N5: J4.pin7, IC1.pin5, IC2.pin5, D1.anode, D3.anode, D6.anode, D8.anode, D9.anode, D11.anode, IC3.pin8
  N6: J3.pin1, IC1.pin6, IC2.pin6, D2.cathode, D4.cathode, D5.cathode, D7.cathode, D10.cathode, D12.cathode
  N7: J3.pin3, IC1.pin17, IC2.pin7
  N8: J3.pin4, IC1.pin19, D3.cathode, D4.anode
  N9: D5.anode, D6.cathode, IC3.pin7
  N10: D7.anode, D8.cathode, IC3.pin6

notes:
  3.3 VDC
  N.C.
  P0.7
  P0.5
  P0.3
  P0.1
  C2CLK
  1
  7
  8
  14
  GND
  P0.6
  P0.4
  P0.2
  P0.0
  /RST
  JTAG/C2
  (lower header)
  (upper header)
  APPLICATION
  TODO: Map TX and RX PiUART to correct MCU pins
